// Logisim project Exo1_TP2.circ as structural Verilog: 1 circuit, main circuit main
module main (
  input  A,
  input  EN_A,
  input  B,
  input  EN_B,
  input  Cin,
  input  F0,
  input  F1,
  output S,
  output Cout
);

  wire _1_2_out, _1_3_out, _1_4_out, _1_5_out, _1_6_out, _1_out, and_1_out, and_2_out, and_3_out, and_4_out,
       and_5_out, and_6_out, and_7_out, and_8_out, and_9_out, and_10_out, and_11_out, Cout_2_out, Cout_out,
       not_1_out, not_2_out, not_3_out, not_4_out, not_5_out, S_2_out, S_3_out, S_4_out, S_out;

  not not_1 (not_1_out, F0);
  and and_1 (and_1_out, A, EN_A);
  not not_2 (not_2_out, F1);
  and and_2 (and_2_out, B, EN_B);
  and and_3 (and_3_out, not_2_out, not_1_out);
  and and_4 (and_4_out, not_2_out, F0);
  and and_5 (and_5_out, F1, F0);
  and and_6 (and_6_out, F1, not_1_out);
  not not_3 (not_3_out, and_1_out);
  xor _1 (_1_out, and_1_out, and_2_out);
  xor _1_2 (_1_2_out, and_1_out, and_2_out);
  and and_7 (and_7_out, Cin, _1_out);
  and and_8 (and_8_out, and_2_out, and_1_out);
  and and_9 (and_9_out, Cin, not_4_out);
  not not_4 (not_4_out, _1_2_out);
  and and_10 (and_10_out, and_2_out, not_3_out);
  and and_11 (and_11_out, and_1_out, and_2_out);
  not not_5 (not_5_out, and_1_out);
  xor _1_3 (_1_3_out, _1_out, Cin);
  xor _1_4 (_1_4_out, _1_2_out, Cin);
  or _1_5 (_1_5_out, and_7_out, and_8_out);
  or _1_6 (_1_6_out, and_9_out, and_10_out);
  and u_S (S_out, and_4_out, and_11_out);
  and S_2 (S_2_out, not_5_out, and_5_out);
  and S_3 (S_3_out, _1_3_out, and_3_out);
  and u_Cout (Cout_out, and_3_out, _1_5_out);
  and S_4 (S_4_out, _1_4_out, and_6_out);
  and Cout_2 (Cout_2_out, and_6_out, _1_6_out);
  or Cout_3 (Cout, Cout_out, Cout_2_out);
  or S_5 (S, S_3_out, S_4_out, S_out, S_2_out);
endmodule
