// Logisim project Exo3_TP2.circ as structural Verilog: 1 circuit, main circuit main
module main (
  input  F0,
  input  EN_A,
  input  EN_B,
  input  A,
  input  A_2,
  input  F1,
  input  A_3,
  input  A_4,
  input  Cin,
  input  B,
  input  B_2,
  input  B_3,
  input  B_4,
  output Cout,
  output S,
  output S_2,
  output S_3,
  output S_4
);

  wire _1_2_out, _1_3_out, _1_4_out, _1_5_out, _1_6_out, _1_7_out, _1_8_out, _1_9_out, _1_10_out, _1_11_out,
       _1_12_out, _1_13_out, _1_14_out, _1_15_out, _1_16_out, _1_17_out, _1_18_out, _1_19_out, _1_20_out,
       _1_21_out, _1_22_out, _1_23_out, _1_24_out, _1_out, A_2_out, A_3_out, A_4_out, A_out, and_2_out,
       and_3_out, and_4_out, and_5_out, and_6_out, and_7_out, and_8_out, and_9_out, and_10_out, and_11_out,
       and_12_out, and_13_out, and_14_out, and_15_out, and_16_out, and_17_out, and_18_out, and_19_out,
       and_20_out, and_21_out, and_22_out, and_23_out, and_24_out, and_25_out, and_26_out, and_27_out,
       and_28_out, and_29_out, and_30_out, and_31_out, and_32_out, and_33_out, and_34_out, and_35_out,
       and_36_out, and_37_out, and_38_out, and_out, B_2_out, B_3_out, B_4_out, B_out, Cout_2_out, Cout_3_out,
       Cout_4_out, Cout_5_out, Cout_6_out, Cout_7_out, Cout_8_out, Cout_9_out, Cout_10_out, Cout_11_out,
       Cout_out, not_1_out, not_2_out, not_3_out, not_4_out, not_5_out, not_6_out, not_7_out, not_8_out,
       not_9_out, not_10_out, not_11_out, not_12_out, not_13_out, not_14_out, not_15_out, not_16_out,
       not_17_out, not_18_out, not_19_out, or_1_out, or_2_out, or_3_out, or_4_out, or_5_out, or_6_out,
       S_2_out, S_3_out, S_4_out, S_5_out, S_6_out, S_7_out, S_8_out, S_9_out, S_10_out, S_11_out, S_12_out,
       S_out, signe_out;

  not not_1 (not_1_out, F0);
  not not_2 (not_2_out, F0);
  not not_3 (not_3_out, and_7_out);
  not not_4 (not_4_out, F1);
  not not_5 (not_5_out, F0);
  not not_6 (not_6_out, F0);
  not not_7 (not_7_out, F1);
  and signe (signe_out, not_3_out, and_6_out);
  not not_8 (not_8_out, and_6_out);
  and \and  (and_out, not_4_out, not_1_out);
  and and_2 (and_2_out, not_4_out, F0);
  and and_3 (and_3_out, F1, F0);
  and and_4 (and_4_out, F1, not_1_out);
  not not_9 (not_9_out, F1);
  not not_10 (not_10_out, F1);
  and and_5 (and_5_out, not_7_out, not_2_out);
  and and_6 (and_6_out, not_7_out, F0);
  and and_7 (and_7_out, F1, F0);
  and and_8 (and_8_out, F1, not_2_out);
  and and_9 (and_9_out, not_9_out, not_5_out);
  and and_10 (and_10_out, not_9_out, F0);
  and and_11 (and_11_out, F1, F0);
  and and_12 (and_12_out, F1, not_5_out);
  and and_13 (and_13_out, not_10_out, not_6_out);
  and and_14 (and_14_out, not_10_out, F0);
  and and_15 (and_15_out, F1, F0);
  and and_16 (and_16_out, F1, not_6_out);
  not not_11 (not_11_out, A_out);
  not not_12 (not_12_out, A_3_out);
  not not_13 (not_13_out, A_2_out);
  not not_14 (not_14_out, A_4_out);
  xor _1 (_1_out, A_out, B_out);
  xor _1_2 (_1_2_out, A_out, B_out);
  or or_1 (or_1_out, and_6_out, and_7_out);
  xor _1_3 (_1_3_out, A_3_out, B_3_out);
  xor _1_4 (_1_4_out, A_3_out, B_3_out);
  not not_15 (not_15_out, _1_4_out);
  or or_2 (or_2_out, and_2_out, and_3_out);
  xor _1_5 (_1_5_out, A_2_out, B_2_out);
  xor _1_6 (_1_6_out, A_2_out, B_2_out);
  or or_3 (or_3_out, and_10_out, and_11_out);
  xor _1_7 (_1_7_out, A_4_out, B_4_out);
  xor _1_8 (_1_8_out, A_4_out, B_4_out);
  or or_4 (or_4_out, and_14_out, and_15_out);
  and and_17 (and_17_out, Cin, _1_out);
  and and_18 (and_18_out, B_out, A_out);
  and and_19 (and_19_out, Cin, not_16_out);
  not not_16 (not_16_out, _1_2_out);
  and and_20 (and_20_out, B_out, not_11_out);
  xor _1_9 (_1_9_out, _1_3_out, Cout_9_out);
  and and_21 (and_21_out, Cout_9_out, _1_3_out);
  and and_22 (and_22_out, B_3_out, A_3_out);
  xor _1_10 (_1_10_out, _1_4_out, Cout_9_out);
  and and_23 (and_23_out, Cout_9_out, not_15_out);
  and and_24 (and_24_out, B_3_out, not_12_out);
  and u_S (S_out, or_6_out, or_2_out);
  and and_25 (and_25_out, B_2_out, A_2_out);
  not not_17 (not_17_out, _1_6_out);
  and and_26 (and_26_out, B_2_out, not_13_out);
  and and_27 (and_27_out, Cout_11_out, _1_7_out);
  and and_28 (and_28_out, B_4_out, A_4_out);
  and and_29 (and_29_out, Cout_11_out, not_18_out);
  not not_18 (not_18_out, _1_8_out);
  and and_30 (and_30_out, B_4_out, not_14_out);
  xor _1_11 (_1_11_out, _1_out, Cin);
  xor _1_12 (_1_12_out, _1_2_out, Cin);
  and u_S_2 (S_2_out, and_37_out, or_1_out);
  xor _1_13 (_1_13_out, _1_5_out, Cout_10_out);
  and and_31 (and_31_out, Cout_10_out, _1_5_out);
  xor _1_14 (_1_14_out, _1_6_out, Cout_10_out);
  and and_32 (and_32_out, Cout_10_out, not_17_out);
  and u_S_3 (S_3_out, or_5_out, or_3_out);
  xor _1_15 (_1_15_out, _1_7_out, Cout_11_out);
  xor _1_16 (_1_16_out, _1_8_out, Cout_11_out);
  and u_S_4 (S_4_out, and_34_out, or_4_out);
  or _1_17 (_1_17_out, and_17_out, and_18_out);
  or _1_18 (_1_18_out, and_19_out, and_20_out);
  or _1_19 (_1_19_out, and_21_out, and_22_out);
  or _1_20 (_1_20_out, and_23_out, and_24_out);
  or _1_21 (_1_21_out, and_31_out, and_25_out);
  or _1_22 (_1_22_out, and_32_out, and_26_out);
  or _1_23 (_1_23_out, and_27_out, and_28_out);
  or _1_24 (_1_24_out, and_29_out, and_30_out);
  and S_5 (S_5_out, _1_11_out, and_5_out);
  and S_6 (S_6_out, _1_9_out, and_out);
  and u_Cout (Cout_out, and_out, _1_19_out);
  and S_7 (S_7_out, _1_10_out, and_4_out);
  and Cout_2 (Cout_2_out, and_4_out, _1_20_out);
  and S_8 (S_8_out, _1_15_out, and_13_out);
  and Cout_3 (Cout_3_out, and_5_out, _1_17_out);
  and S_9 (S_9_out, _1_12_out, and_8_out);
  and Cout_4 (Cout_4_out, and_8_out, _1_18_out);
  and S_10 (S_10_out, _1_13_out, and_9_out);
  and Cout_5 (Cout_5_out, and_9_out, _1_21_out);
  and S_11 (S_11_out, _1_14_out, and_12_out);
  and Cout_6 (Cout_6_out, and_12_out, _1_22_out);
  and Cout_7 (Cout_7_out, and_13_out, _1_23_out);
  and S_12 (S_12_out, _1_16_out, and_16_out);
  and Cout_8 (Cout_8_out, and_16_out, _1_24_out);
  or Cout_9 (Cout_9_out, Cout_3_out, Cout_4_out);
  or Cout_10 (Cout_10_out, Cout_out, Cout_2_out);
  or Cout_11 (Cout_11_out, Cout_5_out, Cout_6_out);
  or Cout_12 (Cout, Cout_7_out, Cout_8_out);
  or S_13 (S_3, S_6_out, S_7_out, S_out);
  or S_14 (S_4, S_5_out, S_9_out, S_2_out);
  or S_15 (S_2, S_10_out, S_11_out, S_3_out);
  or S_16 (S, S_8_out, S_12_out, S_4_out);
  not not_19 (not_19_out, signe_out);
  and and_33 (and_33_out, A_4_out, signe_out);
  and u_A (A_out, A_2, EN_A);
  and and_34 (and_34_out, not_19_out, A_2_out);
  or or_5 (or_5_out, and_33_out, and_36_out);
  and and_35 (and_35_out, A_2_out, signe_out);
  and and_36 (and_36_out, not_19_out, A_3_out);
  and and_37 (and_37_out, A_3_out, signe_out);
  or or_6 (or_6_out, and_35_out, and_38_out);
  and and_38 (and_38_out, not_19_out, A_out);
  and u_B (B_out, B, EN_B);
  and u_A_2 (A_2_out, EN_A, A_3);
  and u_B_2 (B_2_out, B_3, EN_B);
  and u_A_3 (A_3_out, EN_A, A_4);
  and u_B_3 (B_3_out, B_4, EN_B);
  and u_A_4 (A_4_out, EN_A, A);
  and u_B_4 (B_4_out, EN_B, B_2);
endmodule
