// Logisim project Exo1_TP1.circ as structural Verilog: 1 circuit, main circuit main
module main (
  input  A,
  input  B,
  output out_3,
  output out_4
);

  xor _1 (out_3, A, B);
  and \and  (out_4, B, A);
endmodule
