// Logisim project Exo2_TP1.circ as structural Verilog: 1 circuit, main circuit main
module main (
  input  A,
  input  B,
  input  Cin,
  output S,
  output Cout
);

  wire _1_out, and_2_out, and_out;

  xor _1 (_1_out, A, B);
  xor _1_2 (S, _1_out, Cin);
  and \and  (and_out, Cin, _1_out);
  and and_2 (and_2_out, B, A);
  or _1_3 (Cout, and_out, and_2_out);
endmodule
