// Logisim project Exo3_TP1.circ as structural Verilog: 1 circuit, main circuit main
module main (
  input  A,
  input  A_2,
  input  A_3,
  input  A_4,
  input  A_5,
  input  A_6,
  input  A_7,
  input  A_8,
  input  B,
  input  B_2,
  input  B_3,
  input  B_4,
  input  B_5,
  input  B_6,
  input  B_7,
  input  B_8,
  output Cout,
  output S,
  output S_2,
  output S_3,
  output S_4,
  output S_5,
  output S_6,
  output S_7,
  output S_8
);

  wire _1_2_out, _1_3_out, _1_4_out, _1_5_out, _1_6_out, _1_7_out, _1_8_out, _1_17_out, _1_18_out, _1_19_out,
       _1_20_out, _1_21_out, _1_22_out, and_2_out, and_3_out, and_4_out, and_5_out, and_6_out, and_7_out,
       and_8_out, and_9_out, and_10_out, and_11_out, and_12_out, and_13_out, and_14_out, and_15_out, and_out;

  xor _1 (S_8, A_8, B_7);
  and \and  (and_out, B_7, A_8);
  xor _1_2 (_1_2_out, A_7, B_6);
  xor _1_3 (_1_3_out, A_6, B_5);
  xor _1_4 (_1_4_out, A_5, B_4);
  xor _1_5 (_1_5_out, A_4, B_3);
  xor _1_6 (_1_6_out, A_3, B_2);
  xor _1_7 (_1_7_out, A_2, B);
  xor _1_8 (_1_8_out, A, B_8);
  xor _1_9 (S, _1_8_out, _1_22_out);
  and and_2 (and_2_out, _1_22_out, _1_8_out);
  and and_3 (and_3_out, B_8, A);
  xor _1_10 (S_7, _1_2_out, and_out);
  and and_4 (and_4_out, and_out, _1_2_out);
  and and_5 (and_5_out, B_6, A_7);
  xor _1_11 (S_6, _1_3_out, _1_17_out);
  and and_6 (and_6_out, _1_17_out, _1_3_out);
  and and_7 (and_7_out, B_5, A_6);
  xor _1_12 (S_5, _1_4_out, _1_18_out);
  and and_8 (and_8_out, _1_18_out, _1_4_out);
  and and_9 (and_9_out, B_4, A_5);
  xor _1_13 (S_4, _1_5_out, _1_19_out);
  and and_10 (and_10_out, _1_19_out, _1_5_out);
  and and_11 (and_11_out, B_3, A_4);
  xor _1_14 (S_3, _1_6_out, _1_20_out);
  and and_12 (and_12_out, _1_20_out, _1_6_out);
  and and_13 (and_13_out, B_2, A_3);
  xor _1_15 (S_2, _1_7_out, _1_21_out);
  and and_14 (and_14_out, _1_21_out, _1_7_out);
  and and_15 (and_15_out, B, A_2);
  or _1_16 (Cout, and_2_out, and_3_out);
  or _1_17 (_1_17_out, and_4_out, and_5_out);
  or _1_18 (_1_18_out, and_6_out, and_7_out);
  or _1_19 (_1_19_out, and_8_out, and_9_out);
  or _1_20 (_1_20_out, and_10_out, and_11_out);
  or _1_21 (_1_21_out, and_12_out, and_13_out);
  or _1_22 (_1_22_out, and_14_out, and_15_out);
endmodule
