// Logisim project Exo4_TP1.circ as structural Verilog: 1 circuit, main circuit main
module main (
  input  A,
  input  A_2,
  input  A_3,
  input  A_4,
  input  A_5,
  input  A_6,
  input  A_7,
  input  A_8,
  input  B,
  input  B_2,
  input  B_3,
  input  B_4,
  input  B_5,
  input  B_6,
  input  B_7,
  input  B_8,
  output Cout,
  output out_18,
  output S,
  output S_2,
  output S_3,
  output S_4,
  output S_5,
  output S_6,
  output S_7
);

  wire _1_2_out, _1_3_out, _1_4_out, _1_5_out, _1_6_out, _1_7_out, _1_8_out, _1_10_out, _1_12_out, _1_14_out,
       _1_16_out, _1_18_out, _1_20_out, and_2_out, and_3_out, and_4_out, and_5_out, and_6_out, and_7_out,
       and_8_out, and_9_out, and_10_out, and_11_out, and_12_out, and_13_out, and_14_out, and_15_out, and_out,
       not_1_out, not_2_out, not_3_out, not_4_out, not_5_out, not_6_out, not_7_out, not_8_out, not_9_out,
       not_10_out, not_11_out, not_12_out, not_13_out, not_14_out, not_15_out;

  not not_1 (not_1_out, A_8);
  not not_2 (not_2_out, A_7);
  not not_3 (not_3_out, A_6);
  not not_4 (not_4_out, A_5);
  not not_5 (not_5_out, A_4);
  not not_6 (not_6_out, A_3);
  not not_7 (not_7_out, A_2);
  not not_8 (not_8_out, A);
  xor _1 (S_3, A_8, B_8);
  and \and  (and_out, B_8, not_1_out);
  xor _1_2 (_1_2_out, A_7, B_7);
  not not_9 (not_9_out, _1_2_out);
  xor _1_3 (_1_3_out, A_6, B_6);
  not not_10 (not_10_out, _1_3_out);
  xor _1_4 (_1_4_out, A_5, B_5);
  not not_11 (not_11_out, _1_4_out);
  xor _1_5 (_1_5_out, A_4, B_4);
  not not_12 (not_12_out, _1_5_out);
  xor _1_6 (_1_6_out, A_3, B_3);
  not not_13 (not_13_out, _1_6_out);
  xor _1_7 (_1_7_out, A_2, B_2);
  not not_14 (not_14_out, _1_7_out);
  xor _1_8 (_1_8_out, A, B);
  not not_15 (not_15_out, _1_8_out);
  and and_2 (and_2_out, and_out, not_9_out);
  and and_3 (and_3_out, B_7, not_2_out);
  and and_4 (and_4_out, _1_10_out, not_10_out);
  and and_5 (and_5_out, B_6, not_3_out);
  and and_6 (and_6_out, _1_12_out, not_11_out);
  and and_7 (and_7_out, B_5, not_4_out);
  and and_8 (and_8_out, _1_14_out, not_12_out);
  and and_9 (and_9_out, B_4, not_5_out);
  and and_10 (and_10_out, _1_16_out, not_13_out);
  and and_11 (and_11_out, B_3, not_6_out);
  and and_12 (and_12_out, _1_18_out, not_14_out);
  and and_13 (and_13_out, B_2, not_7_out);
  and and_14 (and_14_out, _1_20_out, not_15_out);
  and and_15 (and_15_out, B, not_8_out);
  xor _1_9 (S_7, _1_2_out, and_out);
  or _1_10 (_1_10_out, and_2_out, and_3_out);
  xor _1_11 (S_6, _1_3_out, _1_10_out);
  or _1_12 (_1_12_out, and_4_out, and_5_out);
  xor _1_13 (S_5, _1_4_out, _1_12_out);
  or _1_14 (_1_14_out, and_6_out, and_7_out);
  xor _1_15 (S_4, _1_5_out, _1_14_out);
  or _1_16 (_1_16_out, and_8_out, and_9_out);
  xor _1_17 (S_2, _1_6_out, _1_16_out);
  or _1_18 (_1_18_out, and_10_out, and_11_out);
  xor _1_19 (S, _1_7_out, _1_18_out);
  or _1_20 (_1_20_out, and_12_out, and_13_out);
  xor _1_21 (out_18, _1_8_out, _1_20_out);
  or _1_22 (Cout, and_14_out, and_15_out);
endmodule
