// Logisim project Exo6_TP1.circ as structural Verilog: 1 circuit, main circuit main
module main (
  input  in_1,
  input  in_2,
  input  in_3,
  input  in_4,
  input  in_5,
  input  in_6,
  input  in_7,
  input  in_8,
  input  in_9,
  output Cout,
  output S,
  output S_2,
  output S_3,
  output S_4,
  output S_5,
  output S_6,
  output S_7,
  output S_8
);

  wire _1_2_out, _1_3_out, _1_4_out, _1_5_out, _1_6_out, _1_7_out, _1_8_out, _1_16_out, _1_17_out, _1_18_out,
       _1_19_out, _1_20_out, _1_21_out, and_1_out, and_2_out, and_3_out, and_4_out, and_5_out, and_6_out,
       and_7_out, and_8_out, and_9_out, and_10_out, and_11_out, and_12_out, and_13_out, and_14_out,
       and_15_out, and_16_out, and_17_out, and_18_out, and_19_out, and_20_out, and_21_out, and_22_out,
       and_23_out, and_24_out, and_25_out, and_26_out, and_27_out, and_28_out, and_29_out, and_30_out,
       and_31_out, and_32_out, and_33_out, and_34_out, and_35_out, and_36_out, and_37_out, and_38_out,
       and_39_out, and_40_out, and_41_out, and_42_out, and_43_out, not_1_out, not_2_out, or_1_out, or_2_out,
       or_3_out, or_4_out, or_5_out, or_6_out, or_7_out, or_8_out, or_9_out, or_10_out, or_11_out, or_12_out;

  not not_1 (not_1_out, in_9);
  and and_1 (and_1_out, in_1, in_9);
  not not_2 (not_2_out, in_9);
  and and_2 (and_2_out, and_3_out, in_9);
  and and_3 (and_3_out, not_1_out, in_2);
  or or_1 (or_1_out, and_1_out, and_5_out);
  and and_4 (and_4_out, not_2_out, or_1_out);
  or or_2 (or_2_out, and_2_out, and_8_out);
  and and_5 (and_5_out, not_1_out, in_3);
  and and_6 (and_6_out, in_2, in_9);
  and and_7 (and_7_out, or_1_out, in_9);
  and and_8 (and_8_out, not_2_out, or_3_out);
  and and_9 (and_9_out, in_3, in_9);
  or or_3 (or_3_out, and_6_out, and_12_out);
  and and_10 (and_10_out, or_3_out, in_9);
  or or_4 (or_4_out, and_7_out, and_14_out);
  and and_11 (and_11_out, in_5, in_9);
  and and_12 (and_12_out, not_1_out, in_5);
  or or_5 (or_5_out, and_9_out, and_15_out);
  and and_13 (and_13_out, or_5_out, in_9);
  and and_14 (and_14_out, not_2_out, or_5_out);
  or or_6 (or_6_out, and_10_out, and_16_out);
  and and_15 (and_15_out, not_1_out, in_4);
  or or_7 (or_7_out, and_11_out, and_18_out);
  and and_16 (and_16_out, not_2_out, or_7_out);
  or or_8 (or_8_out, and_13_out, and_19_out);
  and and_17 (and_17_out, in_4, in_9);
  and and_18 (and_18_out, not_1_out, in_6);
  and and_19 (and_19_out, not_2_out, or_9_out);
  and and_20 (and_20_out, or_7_out, in_9);
  and and_21 (and_21_out, in_6, in_9);
  or or_9 (or_9_out, and_17_out, and_23_out);
  and and_22 (and_22_out, or_9_out, in_9);
  or or_10 (or_10_out, and_20_out, and_26_out);
  and and_23 (and_23_out, not_1_out, in_7);
  and and_24 (and_24_out, in_7, in_9);
  or or_11 (or_11_out, and_21_out, and_27_out);
  and and_25 (and_25_out, or_11_out, in_9);
  and and_26 (and_26_out, not_2_out, or_11_out);
  or or_12 (or_12_out, and_22_out, and_28_out);
  and and_27 (and_27_out, not_1_out, in_8);
  and and_28 (and_28_out, not_2_out, and_24_out);
  xor _1 (S_8, in_8, and_25_out);
  and and_29 (and_29_out, and_25_out, in_8);
  xor _1_2 (_1_2_out, in_7, or_12_out);
  xor _1_3 (_1_3_out, in_6, or_10_out);
  xor _1_4 (_1_4_out, in_4, or_8_out);
  xor _1_5 (_1_5_out, in_5, or_6_out);
  xor _1_6 (_1_6_out, in_3, or_4_out);
  xor _1_7 (_1_7_out, in_2, or_2_out);
  xor _1_8 (_1_8_out, in_1, and_4_out);
  xor _1_9 (S_7, _1_2_out, and_29_out);
  and and_30 (and_30_out, and_29_out, _1_2_out);
  and and_31 (and_31_out, or_12_out, in_7);
  xor _1_10 (S_6, _1_3_out, _1_16_out);
  and and_32 (and_32_out, _1_16_out, _1_3_out);
  and and_33 (and_33_out, or_10_out, in_6);
  xor _1_11 (S_5, _1_4_out, _1_17_out);
  and and_34 (and_34_out, _1_17_out, _1_4_out);
  and and_35 (and_35_out, or_8_out, in_4);
  xor _1_12 (S_4, _1_5_out, _1_18_out);
  and and_36 (and_36_out, _1_18_out, _1_5_out);
  and and_37 (and_37_out, or_6_out, in_5);
  xor _1_13 (S_3, _1_6_out, _1_19_out);
  and and_38 (and_38_out, _1_19_out, _1_6_out);
  and and_39 (and_39_out, or_4_out, in_3);
  xor _1_14 (S_2, _1_7_out, _1_20_out);
  and and_40 (and_40_out, _1_20_out, _1_7_out);
  and and_41 (and_41_out, or_2_out, in_2);
  xor _1_15 (S, _1_8_out, _1_21_out);
  and and_42 (and_42_out, _1_21_out, _1_8_out);
  and and_43 (and_43_out, and_4_out, in_1);
  or _1_16 (_1_16_out, and_30_out, and_31_out);
  or _1_17 (_1_17_out, and_32_out, and_33_out);
  or _1_18 (_1_18_out, and_34_out, and_35_out);
  or _1_19 (_1_19_out, and_36_out, and_37_out);
  or _1_20 (_1_20_out, and_38_out, and_39_out);
  or _1_21 (_1_21_out, and_40_out, and_41_out);
  or _1_22 (Cout, and_42_out, and_43_out);
endmodule
