// Logisim project Exo7-b_TP1.circ as structural Verilog: 1 circuit, main circuit main
module main (
  input  A,
  input  B,
  input  C,
  input  D,
  input  A_2,
  input  B_2,
  input  C_2,
  input  D_2,
  input  A_3,
  input  B_3,
  input  C_3,
  input  D_3,
  input  A_4,
  input  B_4,
  input  C_4,
  input  D_4,
  input  A_5,
  input  B_5,
  input  C_5,
  input  D_5,
  input  A_6,
  input  B_6,
  input  C_6,
  input  D_6,
  input  A_7,
  input  B_7,
  input  C_7,
  input  D_7,
  input  A_8,
  input  B_8,
  input  C_8,
  input  D_8,
  input  A_9,
  input  B_9,
  input  C_9,
  input  D_9,
  input  A_10,
  input  B_10,
  input  C_10,
  input  D_10,
  input  A_11,
  input  B_11,
  input  C_11,
  input  D_11,
  input  A_12,
  input  B_12,
  input  C_12,
  input  D_12,
  input  A_13,
  input  B_13,
  input  C_13,
  input  D_13,
  input  A_14,
  input  B_14,
  input  C_14,
  input  D_14,
  input  A_15,
  input  B_15,
  input  C_15,
  input  D_15,
  input  A_16,
  input  B_16,
  input  C_16,
  input  D_16,
  input  in_65,
  input  in_66,
  input  in_67,
  input  in_68,
  output out_69,
  output out_70,
  output out_71,
  output out_72,
  output out_73,
  output out_74,
  output out_75,
  output out_76,
  output out_77,
  output out_78,
  output out_79,
  output out_80,
  output out_81
);

  wire not_1_out, not_2_out, not_3_out, not_4_out, xor_1_out, xor_2_out, xor_3_out, xor_4_out, xor_5_out,
       xor_6_out, xor_7_out, xor_8_out, xor_9_out, xor_11_out, xor_12_out, xor_14_out, xor_15_out,
       xor_16_out, xor_18_out, xor_20_out, xor_21_out, xor_23_out, xor_24_out, xor_26_out, xor_27_out,
       xor_29_out, xor_30_out, xor_31_out, xor_33_out, xor_35_out, xor_36_out, xor_38_out, xor_39_out,
       xor_41_out, xor_42_out, xor_44_out, xor_45_out, xor_47_out, xor_48_out;

  not not_1 (not_1_out, in_65);
  not not_2 (not_2_out, in_66);
  not not_3 (not_3_out, in_67);
  not not_4 (not_4_out, in_68);
  xor xor_1 (xor_1_out, A, xor_3_out);
  // AND_Gate and_1 has open pins: in0=not_4_out, in1=not_4_out, in2=not_3_out, in3=xor_1_out, out=open
  xor xor_2 (xor_2_out, C, D);
  xor xor_3 (xor_3_out, B, xor_2_out);
  xor xor_4 (xor_4_out, A_2, xor_5_out);
  // AND_Gate and_2 has open pins: in3=xor_4_out, out=open
  xor xor_5 (xor_5_out, B_2, xor_6_out);
  xor xor_6 (xor_6_out, C_2, D_2);
  xor xor_7 (xor_7_out, A_3, xor_8_out);
  // AND_Gate and_3 is placed but not wired
  xor xor_8 (xor_8_out, B_3, xor_9_out);
  xor xor_9 (xor_9_out, C_3, D_3);
  xor xor_10 (out_69, A_4, xor_12_out);
  // AND_Gate and_4 is placed but not wired
  xor xor_11 (xor_11_out, C_4, D_4);
  xor xor_12 (xor_12_out, B_4, xor_11_out);
  xor xor_13 (out_70, A_5, xor_14_out);
  // AND_Gate and_5 is placed but not wired
  xor xor_14 (xor_14_out, B_5, xor_15_out);
  xor xor_15 (xor_15_out, C_5, D_5);
  xor xor_16 (xor_16_out, B_6, xor_18_out);
  xor xor_17 (out_71, A_6, xor_16_out);
  // AND_Gate and_6 is placed but not wired
  xor xor_18 (xor_18_out, C_6, D_6);
  xor xor_19 (out_72, A_7, xor_21_out);
  // AND_Gate and_7 is placed but not wired
  xor xor_20 (xor_20_out, C_7, D_7);
  xor xor_21 (xor_21_out, B_7, xor_20_out);
  xor xor_22 (out_73, A_8, xor_23_out);
  // AND_Gate and_8 is placed but not wired
  xor xor_23 (xor_23_out, B_8, xor_24_out);
  xor xor_24 (xor_24_out, C_8, D_8);
  xor xor_25 (out_74, A_9, xor_26_out);
  // AND_Gate and_9 is placed but not wired
  xor xor_26 (xor_26_out, B_9, xor_27_out);
  xor xor_27 (xor_27_out, C_9, D_9);
  xor xor_28 (out_75, A_10, xor_29_out);
  // AND_Gate and_10 is placed but not wired
  xor xor_29 (xor_29_out, B_10, xor_30_out);
  xor xor_30 (xor_30_out, C_10, D_10);
  xor xor_31 (xor_31_out, B_11, xor_33_out);
  xor xor_32 (out_76, A_11, xor_31_out);
  // AND_Gate and_11 is placed but not wired
  xor xor_33 (xor_33_out, C_11, D_11);
  xor xor_34 (out_77, A_12, xor_35_out);
  // AND_Gate and_12 is placed but not wired
  xor xor_35 (xor_35_out, B_12, xor_36_out);
  xor xor_36 (xor_36_out, C_12, D_12);
  xor xor_37 (out_78, A_13, xor_38_out);
  // AND_Gate and_13 is placed but not wired
  xor xor_38 (xor_38_out, B_13, xor_39_out);
  xor xor_39 (xor_39_out, C_13, D_13);
  xor xor_40 (out_79, A_14, xor_42_out);
  // AND_Gate and_14 is placed but not wired
  xor xor_41 (xor_41_out, C_14, D_14);
  xor xor_42 (xor_42_out, B_14, xor_41_out);
  xor xor_43 (out_80, A_15, xor_44_out);
  // AND_Gate and_15 is placed but not wired
  xor xor_44 (xor_44_out, B_15, xor_45_out);
  xor xor_45 (xor_45_out, C_15, D_15);
  xor xor_46 (out_81, A_16, xor_47_out);
  // AND_Gate and_16 is placed but not wired
  xor xor_47 (xor_47_out, B_16, xor_48_out);
  xor xor_48 (xor_48_out, C_16, D_16);
endmodule
