// Logisim project Exo7_TP1.circ as structural Verilog: 1 circuit, main circuit main
module main (
  input  A,
  input  B,
  input  C,
  input  D,
  output out_5
);

  wire xor_2_out, xor_3_out;

  xor xor_1 (out_5, A, xor_2_out);
  xor xor_2 (xor_2_out, B, xor_3_out);
  xor xor_3 (xor_3_out, C, D);
endmodule
